# Fritzing sketch pcb-in-a-box (saved by Fritzing 0.7.12b)
breadboards: 1

parts:
  Arduino1 = Arduino
  R1 = Rotary Potentiometer (Large) [maximum_resistance=100kΩ package=THT]
  R2 = Rotary Potentiometer (Large) [maximum_resistance=100kΩ package=THT]
  R4 = Trimmer Potentiometer [maximum_resistance=10kΩ package=THT]
  LCD1 = LCD screen
  LED1 = Blue LED - 5mm
  LED2 = Blue LED - 5mm
  LED3 = Blue LED - 5mm
  LED4 = Blue LED - 5mm
  LED5 = Blue LED - 5mm
  LED6 = Blue LED - 5mm
  R7 = 10 Ω Resistor [package=THT]
  R8 = 10 Ω Resistor [package=THT]
  LED7 = green LED - 5mm
  LED8 = LED - 5mm [color="Red (633nm)" package="5 mm [THT]"]
  S1 = Pushbutton [package="[THT]"]
  S2 = Pushbutton [package="[THT]"]
  R5 = 1k Ω Resistor [package=THT]
  R6 = 1k Ω Resistor [package=THT]
  Q1 = pnp-Transistor [package="TO92 [THT]"]
  R9 = 1k Ω Resistor [package=THT]
  Power_plug1 = Power plug
  R10 = 1k Ω Resistor [package=THT]
  Q2 = pnp-Transistor [package="TO92 [THT]"]

nets:
  GND: Arduino1.GND, R5.Pin_0, R6.Pin_0, Power_plug1.GND
  N1: Arduino1.D13, S1.Pin_3, S1.Pin_4
  N2: Arduino1.D12, Arduino1.D11, R7.Pin_0, R8.Pin_0
  N3: Arduino1.D10, R10.Pin_0
  N4: Arduino1.D9, R9.Pin_0
  N5: Arduino1.D8, S2.Pin_3, S2.Pin_4
  N6: Arduino1.D7, LCD1.RS
  N7: Arduino1.D6, LCD1.E
  N8: Arduino1.D5, LCD1.DB4
  N9: Arduino1.D4, LCD1.DB5
  N10: Arduino1.D3, LCD1.DB6
  N11: Arduino1.D2, LCD1.DB7
  N12: Arduino1.A0, R1.wiper
  N13: Arduino1.A1, R2.wiper
  N14: R1.leg1, R2.leg1, R4.leg1, LCD1.VDD, LCD1.LED+
  N15: R2.leg2, R4.leg2, LCD1.VSS, LCD1.R/W, LCD1.LED-, LED7.cathode, LED8.cathode, S1.Pin_1, S1.Pin_2, S2.Pin_1, S2.Pin_2
  N16: R4.wiper, LCD1.V0
  N17: LED1.cathode, LED2.cathode, LED3.cathode, R6.Pin_1
  N18: LED1.anode, LED2.anode, LED3.anode, Q2.collector
  N19: LED4.cathode, LED5.cathode, LED6.cathode, R5.Pin_1
  N20: LED4.anode, LED5.anode, LED6.anode, Q1.collector
  N21: R7.Pin_1, LED8.anode
  N22: R8.Pin_1, LED7.anode
  N23: Q1.emmitter, Power_plug1.VCC, Q2.emmitter
  N24: Q1.base, R9.Pin_1
  N25: R10.Pin_1, Q2.base

notes:
  Nesta Versão ainda falta calcular os valores dos compoentes.
  Porque Potenciometros?
  Os Potenciomentros é uma segunda proposta substituindo os botões que selecionam a intencidade da luz e o tempo.
  LCD
  Usado um LCD Comum
  Não temos ainda um LCD i2C
